# Fritzing sketch sketch (saved by Fritzing 0.8.3b)
breadboards: 1

parts:
  Part1 = Arduino Uno (Rev3)
  LCD1 = LCD screen
  RE1 = Rotary Encoder [package=THT]
  S1 = Pushbutton [package="[THT]"]
  S2 = Pushbutton [package="[THT]"]
  S3 = Pushbutton [package="[THT]"]
  S4 = Pushbutton [package="[THT]"]
  S5 = Pushbutton [package="[THT]"]
  S6 = Pushbutton [package="[THT]"]
  S7 = Pushbutton [package="[THT]"]
  S8 = Pushbutton [package="[THT]"]

nets:
  GND: Part1.GND, LCD1.VSS, LCD1.R/W, LCD1.LED-, RE1.EncoderPinB, S1.Pin_3, S1.Pin_4, S2.Pin_3, S2.Pin_4, S3.Pin_3, S3.Pin_4, S4.Pin_3, S4.Pin_4, S5.Pin_3, S5.Pin_4, S6.Pin_3, S6.Pin_4, S7.Pin_3, S7.Pin_4, S8.Pin_3, S8.Pin_4
  N1: Part1.D8, LCD1.RS
  N2: Part1.D9_PWM, LCD1.E
  N3: Part1.D10_PWM/SS, LCD1.DB4
  N4: Part1.D11_PWM/MOSI, LCD1.DB5
  N5: Part1.D12/MISO, LCD1.DB6
  N6: Part1.D13/SCK, LCD1.DB7
  N7: Part1.D0/RX, S8.Pin_1, S8.Pin_2
  N8: Part1.D1/TX, S7.Pin_1, S7.Pin_2
  N9: Part1.D2, S6.Pin_1, S6.Pin_2
  N10: Part1.D3_PWM, S5.Pin_1, S5.Pin_2
  N11: Part1.D4, S4.Pin_1, S4.Pin_2
  N12: Part1.D5_PWM, S3.Pin_1, S3.Pin_2
  N13: Part1.D6_PWM, S2.Pin_1, S2.Pin_2
  N14: Part1.D7, S1.Pin_1, S1.Pin_2
  5V: Part1.5V, LCD1.VDD, LCD1.LED+, RE1.EncoderPinA
  N15: LCD1.V0, RE1.EncoderPinC
